// Logisim project Miniproject.circ as structural Verilog: 6 circuits, main circuit main
module main (
);

  wire Entry_1_out, Entry_2_out, Entry_3_out, Entry_4_out, Exit_1_out, Exit_2_out, Exit_3_out, Exit_4_out,
       parking_availability_1__1, parking_availability_1__2, parking_availability_1__3,
       parking_availability_1__4, t_ff_1_qn, t_ff_2_qn, t_ff_3_qn, t_ff_4_qn;
  wire [3:0] pay_while_exit_1_tens, pay_while_exit_1_units, pay_while_exit_2_tens, pay_while_exit_2_units,
       pay_while_exit_3_tens, pay_while_exit_3_units, pay_while_exit_4_tens, pay_while_exit_4_units;

  LED led_1 (.in(parking_availability_1__1));
  T_Flip_Flop t_ff_1 (.Qn(t_ff_1_qn), .preset(Exit_1_out), .reset(Entry_1_out));  // open: clk, T, Q, en
  Button Entry_1 (.out(Entry_1_out));
  T_Flip_Flop t_ff_2 (.Qn(t_ff_2_qn), .preset(Exit_2_out), .reset(Entry_2_out));  // open: clk, T, Q, en
  LED led_2 (.in(parking_availability_1__2));
  Button Entry_2 (.out(Entry_2_out));
  PAY_WHILE_EXIT pay_while_exit_1 (.RESET(t_ff_1_qn), .UNITS(pay_while_exit_1_units), .TENS(pay_while_exit_1_tens));
  PAY_WHILE_EXIT pay_while_exit_2 (.RESET(t_ff_2_qn), .UNITS(pay_while_exit_2_units), .TENS(pay_while_exit_2_tens));
  PAY_WHILE_EXIT pay_while_exit_3 (.RESET(t_ff_3_qn), .UNITS(pay_while_exit_3_units), .TENS(pay_while_exit_3_tens));
  PAY_WHILE_EXIT pay_while_exit_4 (.RESET(t_ff_4_qn), .UNITS(pay_while_exit_4_units), .TENS(pay_while_exit_4_tens));
  PARKING_AVAILABILITY parking_availability_1 (
    .X(t_ff_1_qn), .Y(t_ff_2_qn), .Z(t_ff_3_qn), .W(t_ff_4_qn), ._1(parking_availability_1__1),
    ._2(parking_availability_1__2), ._3(parking_availability_1__3), ._4(parking_availability_1__4));
  LED led_3 (.in(parking_availability_1__3));
  Button Entry_3 (.out(Entry_3_out));
  T_Flip_Flop t_ff_3 (.Qn(t_ff_3_qn), .preset(Exit_3_out), .reset(Entry_3_out));  // open: clk, T, Q, en
  T_Flip_Flop t_ff_4 (.Qn(t_ff_4_qn), .preset(Exit_4_out), .reset(Entry_4_out));  // open: clk, T, Q, en
  LED led_4 (.in(parking_availability_1__4));
  Button Entry_4 (.out(Entry_4_out));
  Hex_Digit_Display hex_digit_display_1 (.value(pay_while_exit_1_tens));  // open: dp
  Hex_Digit_Display hex_digit_display_2 (.value(pay_while_exit_2_tens));  // open: dp
  Hex_Digit_Display hex_digit_display_3 (.value(pay_while_exit_3_tens));  // open: dp
  Hex_Digit_Display hex_digit_display_4 (.value(pay_while_exit_4_tens));  // open: dp
  Button Exit_1 (.out(Exit_1_out));
  Hex_Digit_Display hex_digit_display_5 (.value(pay_while_exit_1_units));  // open: dp
  Hex_Digit_Display hex_digit_display_6 (.value(pay_while_exit_2_units));  // open: dp
  Hex_Digit_Display hex_digit_display_7 (.value(pay_while_exit_3_units));  // open: dp
  Hex_Digit_Display hex_digit_display_8 (.value(pay_while_exit_4_units));  // open: dp
  Button Exit_2 (.out(Exit_2_out));
  Button Exit_3 (.out(Exit_3_out));
  Button Exit_4 (.out(Exit_4_out));

  // Notes on the sheet:
  //   Calculates the amount to be paid
  //   CAR PARKING LOT TICKET SYSTEM
  //   Parking availability selector
  //   Availbility updater
  //   LED showing the parking lot to be assigned
  //   Button to select the parking lot
  //   Instructions : 
  //   AMOUNT REQUIRED TO PAY
  //   Press the availability selectors before start to enable them
  //   Button to exit
endmodule

module CLOCK (
  input  RESET,
  output [2:0] OUTPUT_TIME
);

  wire not_1_out, PULSE_out;
  wire [2:0] adder_1_out;

  Clock PULSE (.out(PULSE_out));
  Adder #(.width(3)) adder_1 (.a(OUTPUT_TIME), .b(3'b001), .out(adder_1_out));  // open: cin, cout
  not not_1 (not_1_out, RESET);
  Register #(.width(3)) register_1 (.D(adder_1_out), .Q(OUTPUT_TIME), .clk(PULSE_out), .clr(not_1_out));  // open: en

  // Notes on the sheet:
  //   Updater
  //   Reset triggers clock
  //   Storage for time
endmodule

module PARKING_AVAILABILITY (
  input  X,
  input  Y,
  input  Z,
  input  W,
  output _1,
  output _2,
  output _3,
  output _4
);

  wire not_1_out, not_2_out, not_3_out, xor_2_out, xor_3_out, xor_4_out;

  xor xor_1 (_1, X, 1'b1);
  xor xor_2 (xor_2_out, Y, 1'b1);
  xor xor_3 (xor_3_out, Z, 1'b1);
  xor xor_4 (xor_4_out, 1'b1, W);
  not not_1 (not_1_out, _1);
  not not_2 (not_2_out, xor_2_out);
  not not_3 (not_3_out, xor_3_out);
  and and_1 (_2, not_1_out, xor_2_out);
  and and_2 (_3, not_1_out, not_2_out, xor_3_out);
  and and_3 (_4, not_2_out, not_1_out, not_3_out, xor_4_out);

  // Notes on the sheet:
  //   PARKING AVAILABILITY
  //   The outputs 1 ,2 , 3 , 4  are used to switch on the LED for availability
  //   The inputs X,Y,Z,W correspond to the buttons to be selected
endmodule

module COST_MULTIPLIER (
  input  [2:0] TIME,
  output [3:0] UNITS,
  output [3:0] TENS
);

  wire [2:0] multiplier_1_cout, multiplier_1_out;

  Multiplier #(.width(3)) multiplier_1 (
    .a(3'b010), .b(TIME), .out(multiplier_1_out), .cout(multiplier_1_cout));  // open: cin
  BINARY_TO_BCD binary_to_bcd_1 (
    .A(multiplier_1_cout[0]), .B(multiplier_1_out[2]), .C(multiplier_1_out[1]), .D(multiplier_1_out[0]),
    .B3(UNITS[3]), .B2(UNITS[2]), .B1(UNITS[1]), .B0(UNITS[0]), .B4(TENS[0]));

  assign TENS[3:1] = 3'b000;

  // Notes on the sheet:
  //   Cost
  //   Multiplier
  //   Binary to BCD
endmodule

module PAY_WHILE_EXIT (
  input  RESET,
  output [3:0] UNITS,
  output [3:0] TENS
);

  wire clock_2_out;
  wire [2:0] Clock_output_time, register_1_q;

  CLOCK Clock (.RESET(RESET), .OUTPUT_TIME(Clock_output_time));
  Register #(.width(3)) register_1 (.D(Clock_output_time), .Q(register_1_q), .clk(clock_2_out));  // open: en, clr
  Clock clock_2 (.out(clock_2_out));
  COST_MULTIPLIER Multiplier (.TIME(register_1_q), .UNITS(UNITS), .TENS(TENS));

  // Notes on the sheet:
  //   Calculates the cost for changing time on reset
endmodule

module BINARY_TO_BCD (
  input  A,
  input  B,
  input  C,
  input  D,
  output B3,
  output B2,
  output B1,
  output B0,
  output B4
);

  wire and_1_out, and_2_out, and_4_out, and_5_out, and_6_out, and_7_out, not_1_out, not_2_out, not_3_out,
       not_4_out;

  not not_1 (not_1_out, C);
  not not_2 (not_2_out, C);
  and and_1 (and_1_out, C, B);
  and and_2 (and_2_out, not_1_out, A, B);
  not not_3 (not_3_out, A);
  not not_4 (not_4_out, B);
  and and_3 (B3, A, not_2_out, not_4_out);
  and and_4 (and_4_out, not_3_out, B);
  and and_5 (and_5_out, not_3_out, C);
  and and_6 (and_6_out, B, A);
  or or_1 (B4, and_6_out, and_7_out);
  and and_7 (and_7_out, A, C);
  or or_2 (B2, and_1_out, and_4_out);
  or or_3 (B1, and_5_out, and_2_out);

  assign B0 = D;

  // Notes on the sheet:
  //   4 bit binary ABCD to B4 B3 B2 B1 B0 BCD form
endmodule
